// Logisim project cpu.circ as structural Verilog: 3 circuits, main circuit main
module main (
  input  [31:0] INSTRUCTION,
  input  CLOCK,
  output [31:0] FETCH_ADDRESS,
  output [31:0] s0_Value,
  output [31:0] s1_Value,
  output [31:0] s2_Value,
  output [31:0] ra_Value,
  output [31:0] sp_Value,
  output [31:0] out_9,
  output [31:0] out_10,
  output [4:0] out_11,
  output [31:0] out_12,
  output [3:0] out_13,
  output [31:0] out_14
);

  wire ALUsrc, ExtOp, Jump, LuiO, main_2_signed_overflow, main_3_p1, main_3_p3, main_3_p9, MemtoReg,
       MemWrite, nPCsel, RegDst, RegWrite;
  wire [4:0] multiplexer_2_out;
  wire [31:0] adder_1_out, adder_2_out, bit_extender_1_out, bit_extender_2_out, bit_extender_3_out, busB,
       main_2_result, main_3_p11, multiplexer_1_out, multiplexer_5_out, shifter_1_out;

  assign bit_extender_1_out = {{16{INSTRUCTION[15]}}, INSTRUCTION[15:0]};  // Bit_Extender bit_extender_1
  Adder #(.width(32)) adder_1 (.a(32'h4), .b(FETCH_ADDRESS), .out(adder_1_out));  // open: cin, cout
  Adder #(.width(32)) adder_2 (.a(adder_1_out), .b(bit_extender_1_out), .out(adder_2_out));  // open: cin, cout
  Multiplexer #(.width(32)) multiplexer_1 (
    .in0(adder_1_out), .in1(adder_2_out), .out(multiplexer_1_out), .sel(nPCsel));  // open: en
  Register #(.width(32)) PC (.D(multiplexer_1_out), .Q(FETCH_ADDRESS), .clk(CLOCK));  // open: en, clr
  Control control_1 (
    .in(INSTRUCTION), .RegDst(RegDst), .ALUSrc(ALUsrc), .MemtoReg(MemtoReg), .RegWrite(RegWrite),
    .MemWrite(MemWrite), .nPCsel(nPCsel), .Jump(Jump), .ExtOp(ExtOp), .luiO(LuiO), .ALUctr(out_13));
  Multiplexer #(.width(5)) multiplexer_2 (
    .in0(INSTRUCTION[20:16]), .in1(INSTRUCTION[15:11]), .out(multiplexer_2_out), .sel(RegDst));  // open: en
  regfile_main main_1 (
    .Read_Register_1(INSTRUCTION[25:21]), .Read_Register_2(INSTRUCTION[20:16]),
    .Write_Register(multiplexer_2_out), .Write_Data(out_12), .Write_Enable(RegWrite), .Clock(CLOCK),
    .Read_Data_1(out_10), .Read_Data_2(busB), .s0_Value(s0_Value), .s1_Value(s1_Value), .s2_Value(s2_Value),
    .ra_Value(ra_Value), .sp_Value(sp_Value));
  assign bit_extender_2_out = {{16{1'b0}}, INSTRUCTION[15:0]};  // Bit_Extender bit_extender_2
  assign bit_extender_3_out = {{16{INSTRUCTION[15]}}, INSTRUCTION[15:0]};  // Bit_Extender bit_extender_3
  Multiplexer #(.width(32)) multiplexer_3 (
    .in0(bit_extender_2_out), .in1(bit_extender_3_out), .out(out_9), .sel(ExtOp));  // open: en
  Multiplexer #(.width(32)) multiplexer_4 (.in0(busB), .in1(out_9), .out(out_14), .sel(ALUsrc));  // open: en
  LED led_1 (.in(main_2_signed_overflow));
  alu_main main_2 (
    .Switch(out_13), .X(out_10), .Result(main_2_result), .Signed_Overflow(main_2_signed_overflow), .Y(out_14));  // open: Equal
  Shifter #(.width(32)) shifter_1 (.in(out_9), .\dist (5'b10000), .out(shifter_1_out));
  Multiplexer #(.width(32)) multiplexer_5 (
    .in0(main_2_result), .in1(shifter_1_out), .out(multiplexer_5_out), .sel(LuiO));  // open: en
  // mem_main main_3: pin names not known; wires that end beside it: main_3_p1, main_3_p1, main_3_p3, main_3_p3, main_2_result, busB, MemWrite, busB, main_3_p9, CLOCK, main_3_p11, out_9
  Multiplexer #(.width(32)) multiplexer_6 (
    .in0(multiplexer_5_out), .in1(main_3_p11), .out(out_12), .sel(MemtoReg));  // open: en

  assign out_11 = INSTRUCTION[20:16];

  // Other names for the same wires on the sheet: ALUctr[3:0] = out_13; busA[31:0] = out_10; busW[31:0] = out_12;
  //   clk = CLOCK; fetch_addr[31:0] = FETCH_ADDRESS; immExt[31:0] = out_9; imm[15:0] = INSTRUCTION[15:0];
  //   rd[4:0] = INSTRUCTION[15:11]; rt[4:0] = INSTRUCTION[20:16]; rs[4:0] = INSTRUCTION[25:21]; ra[31:0] = ra_Value;
  //   s0[31:0] = s0_Value; s1[31:0] = s1_Value; s2[31:0] = s2_Value; sp[31:0] = sp_Value

  // Notes on the sheet:
  //   Output
  //   These are outputs/inputs from run.circ
  //   Inputs
  //   These are DEBUG/TEST outputs from your circuit.
endmodule

module Control2 (
  input  [31:0] in,
  output [11:0] out_2,
  output out_3,
  output out_4,
  output out_5,
  output out_6,
  output out_7,
  output out_8,
  output out_9,
  output out_10,
  output [3:0] out_11
);

  wire undriven;
  wire [11:0] multiplexer_1_out, multiplexer_3_out, multiplexer_4_out, multiplexer_5_out;
  wire [31:0] shifter_1_out;

  Shifter #(.width(32)) shifter_1 (.in(in), .\dist (5'b11010), .out(shifter_1_out));
  Multiplexer #(.select(5), .width(12)) multiplexer_1 (
    .in0(12'h90), .in3(12'h290), .out(multiplexer_1_out), .sel(in[4:0]));  // open: in1, in2, in4, in5, in6, in7, in8, in9, in10, in11, in12, in13, in14, in15, in16, in17, in18, in19, in20, in21, in22, in23, in24, in25, in26, in27, in28, in29, in30, in31, en
  Multiplexer #(.width(12)) multiplexer_2 (
    .in0(multiplexer_1_out), .in1(multiplexer_3_out), .out(out_2), .sel(in[5]), .en(undriven));
  Multiplexer #(.select(5), .width(12)) multiplexer_3 (
    .in0(12'h590), .in1(12'h690), .in4(12'h990), .in5(12'ha90), .in10(12'hb90), .in11(12'hc90),
    .out(multiplexer_3_out), .sel(in[4:0]));  // open: in2, in3, in6, in7, in8, in9, in12, in13, in14, in15, in16, in17, in18, in19, in20, in21, in22, in23, in24, in25, in26, in27, in28, in29, in30, in31, en
  Multiplexer #(.select(5), .width(12)) multiplexer_4 (
    .in0(out_2), .in1(out_2), .out(multiplexer_4_out), .sel(shifter_1_out[4:0]));  // open: in2, in3, in4, in5, in6, in7, in8, in9, in10, in11, in12, in13, in14, in15, in16, in17, in18, in19, in20, in21, in22, in23, in24, in25, in26, in27, in28, in29, in30, in31, en
  Multiplexer #(.select(5), .width(12)) multiplexer_5 (
    .out(multiplexer_5_out), .sel(shifter_1_out[4:0]));  // open: in0, in1, in2, in3, in4, in5, in6, in7, in8, in9, in10, in11, in12, in13, in14, in15, in16, in17, in18, in19, in20, in21, in22, in23, in24, in25, in26, in27, in28, in29, in30, in31, en
  Multiplexer #(.width(12)) multiplexer_6 (
    .in0(multiplexer_4_out), .in1(multiplexer_5_out),
    .out({out_11, out_10, out_9, out_8, out_7, out_6, out_5, out_4, out_3}), .sel(shifter_1_out[5]));  // open: en
endmodule

module Control (
  input  [31:0] in,
  output RegDst,
  output ALUSrc,
  output MemtoReg,
  output RegWrite,
  output MemWrite,
  output nPCsel,
  output Jump,
  output ExtOp,
  output luiO,
  output [3:0] ALUctr
);

  wire add, addi, addiu, addu, \and , andi, beq, bne, comparator_13_eq, comparator_14_eq, comparator_15_eq,
       comparator_16_eq, comparator_17_eq, comparator_18_eq, comparator_19_eq, comparator_20_eq,
       comparator_21_eq, comparator_22_eq, comparator_23_eq, j, jal, jr, lui, lw, \or , or_1_out, or_2_out,
       or_3_out, or_4_out, or_6_out, ori, rtype, slt, slti, sltu, sra, srl, sub, subu;
  wire [3:0] multiplexer_1_out, multiplexer_2_out, multiplexer_3_out, multiplexer_4_out, multiplexer_5_out,
       multiplexer_6_out, multiplexer_7_out, multiplexer_8_out, multiplexer_9_out;

  Comparator #(.width(6), .mode("unsigned")) comparator_1 (.a(in[31:26]), .b({6{1'b0}}), .eq(rtype));  // open: gt, lt
  Comparator #(.width(6), .mode("unsigned")) comparator_2 (.a(in[31:26]), .b(6'b001000), .eq(addi));  // open: gt, lt
  Comparator #(.width(6), .mode("unsigned")) comparator_3 (.a(in[31:26]), .b(6'b001001), .eq(addiu));  // open: gt, lt
  Comparator #(.width(6), .mode("unsigned")) comparator_4 (.a(in[31:26]), .b(6'b001100), .eq(andi));  // open: gt, lt
  Comparator #(.width(6), .mode("unsigned")) comparator_5 (.a(in[31:26]), .eq(beq));  // open: b, gt, lt
  Comparator #(.width(6), .mode("unsigned")) comparator_6 (.a(in[31:26]), .eq(bne));  // open: b, gt, lt
  Comparator #(.width(6), .mode("unsigned")) comparator_7 (.a(in[31:26]), .eq(j));  // open: b, gt, lt
  Comparator #(.width(6), .mode("unsigned")) comparator_8 (.a(in[31:26]), .eq(jal));  // open: b, gt, lt
  Comparator #(.width(6), .mode("unsigned")) comparator_9 (.a(in[31:26]), .b(6'b001111), .eq(lui));  // open: gt, lt
  Comparator #(.width(6), .mode("unsigned")) comparator_10 (.a(in[31:26]), .eq(lw));  // open: b, gt, lt
  Comparator #(.width(6), .mode("unsigned")) comparator_11 (.a(in[31:26]), .b(6'b001101), .eq(ori));  // open: gt, lt
  Comparator #(.width(6), .mode("unsigned")) comparator_12 (.a(in[31:26]), .b(6'b001010), .eq(slti));  // open: gt, lt
  Comparator #(.width(6), .mode("unsigned")) comparator_13 (
    .a(in[5:0]), .b(6'b100000), .eq(comparator_13_eq));  // open: gt, lt
  Comparator #(.width(6), .mode("unsigned")) comparator_14 (
    .a(in[5:0]), .b(6'b000010), .eq(comparator_14_eq));  // open: gt, lt
  Comparator #(.width(6), .mode("unsigned")) comparator_15 (
    .a(in[5:0]), .b(6'b000011), .eq(comparator_15_eq));  // open: gt, lt
  Comparator #(.width(6), .mode("unsigned")) comparator_16 (
    .a(in[5:0]), .b(6'b100001), .eq(comparator_16_eq));  // open: gt, lt
  Comparator #(.width(6), .mode("unsigned")) comparator_17 (
    .a(in[5:0]), .b(6'b100010), .eq(comparator_17_eq));  // open: gt, lt
  Comparator #(.width(6), .mode("unsigned")) comparator_18 (
    .a(in[5:0]), .b(6'b100011), .eq(comparator_18_eq));  // open: gt, lt
  Comparator #(.width(6), .mode("unsigned")) comparator_19 (
    .a(in[5:0]), .b(6'b100100), .eq(comparator_19_eq));  // open: gt, lt
  Comparator #(.width(6), .mode("unsigned")) comparator_20 (
    .a(in[5:0]), .b(6'b100101), .eq(comparator_20_eq));  // open: gt, lt
  Comparator #(.width(6), .mode("unsigned")) comparator_21 (
    .a(in[5:0]), .b(6'b101010), .eq(comparator_21_eq));  // open: gt, lt
  Comparator #(.width(6), .mode("unsigned")) comparator_22 (
    .a(in[5:0]), .b(6'b101011), .eq(comparator_22_eq));  // open: gt, lt
  Comparator #(.width(6), .mode("unsigned")) comparator_23 (
    .a(in[5:0]), .b(6'b001000), .eq(comparator_23_eq));  // open: gt, lt
  and and_1 (add, rtype, comparator_13_eq);
  and and_2 (srl, rtype, comparator_14_eq);
  and and_3 (sra, rtype, comparator_15_eq);
  and and_4 (addu, rtype, comparator_16_eq);
  and and_5 (sub, rtype, comparator_17_eq);
  and and_6 (subu, rtype, comparator_18_eq);
  and and_7 (\and , rtype, comparator_19_eq);
  and and_8 (\or , rtype, comparator_20_eq);
  and and_9 (slt, rtype, comparator_21_eq);
  and and_10 (sltu, rtype, comparator_22_eq);
  and and_11 (jr, rtype, comparator_23_eq);
  Multiplexer #(.width(4)) multiplexer_1 (
    .in0(4'b0000), .in1(4'b0001), .out(multiplexer_1_out), .sel(srl));  // open: en
  Multiplexer #(.width(4)) multiplexer_2 (
    .in0(multiplexer_1_out), .in1(4'b0010), .out(multiplexer_2_out), .sel(sra));  // open: en
  Multiplexer #(.width(4)) multiplexer_3 (
    .in0(multiplexer_2_out), .in1(4'b0101), .out(multiplexer_3_out), .sel(or_2_out));  // open: en
  or or_1 (or_1_out, addu, addiu);
  or or_2 (or_2_out, add, addi);
  Multiplexer #(.width(4)) multiplexer_4 (
    .in0(multiplexer_3_out), .in1(4'b0110), .out(multiplexer_4_out), .sel(or_1_out));  // open: en
  Multiplexer #(.width(4)) multiplexer_5 (
    .in0(multiplexer_4_out), .in1(4'b0111), .out(multiplexer_5_out), .sel(sub));  // open: en
  Multiplexer #(.width(4)) multiplexer_6 (
    .in0(multiplexer_5_out), .in1(4'b1000), .out(multiplexer_6_out), .sel(subu));  // open: en
  Multiplexer #(.width(4)) multiplexer_7 (
    .in0(multiplexer_6_out), .in1(4'b1001), .out(multiplexer_7_out), .sel(or_4_out));  // open: en
  or or_3 (or_3_out, \or , ori);
  or or_4 (or_4_out, \and , andi);
  or or_5 (RegWrite, rtype, addi, addiu, andi, lui, ori, slti);
  Multiplexer #(.width(4)) multiplexer_8 (
    .in0(multiplexer_7_out), .in1(4'b1010), .out(multiplexer_8_out), .sel(or_3_out));  // open: en
  Multiplexer #(.width(4)) multiplexer_9 (
    .in0(multiplexer_8_out), .in1(4'b1011), .out(multiplexer_9_out), .sel(or_6_out));  // open: en
  or or_6 (or_6_out, slt, slti);
  buf or_7 (RegDst, rtype);  // OR_Gate
  or or_8 (ALUSrc, addi, addiu, andi, lui, ori, slti);
  buf or_9 (MemtoReg, 1'b0);  // OR_Gate
  buf or_10 (MemWrite, 1'b0);  // OR_Gate
  buf or_11 (nPCsel, 1'b0);  // OR_Gate
  buf or_12 (Jump, 1'b0);  // OR_Gate
  buf or_13 (ExtOp, addi);  // OR_Gate
  buf or_14 (luiO, lui);  // OR_Gate
  Multiplexer #(.width(4)) multiplexer_10 (
    .in0(multiplexer_9_out), .in1(4'b1100), .out(ALUctr), .sel(sltu));  // open: en

  // Other names for the same wires on the sheet: funcO[5:0] = in[5:0]; opcode[5:0] = in[31:26]
endmodule
