// Logisim project regfile.circ as structural Verilog: 1 circuit, main circuit main
module main (
  input  [4:0] Read_Register_1,
  input  [4:0] Read_Register_2,
  input  [4:0] Write_Register,
  input  [31:0] Write_Data,
  input  Write_Enable,
  input  Clock,
  output [31:0] s0_Value,
  output [31:0] s1_Value,
  output [31:0] s2_Value,
  output [31:0] ra_Value,
  output [31:0] sp_Value,
  output [31:0] Read_Data_1,
  output [31:0] Read_Data_2
);

  wire [31:0] a0, a1, a2, a3, at, fp, gp, k0, k1, RW, s3, s4, s5, s6, s7, t0, t1, t2, t3, t4, t5, t6, t7, t8,
       t9, v0, v1;

  Demultiplexer #(.select(5), .width(32)) demultiplexer_1 (
    .out1(at), .out2(v0), .out3(v1), .out4(a0), .out5(a1), .out6(a2), .out7(a3), .out8(t0), .out9(t1),
    .in(Write_Data), .sel(Write_Register));  // open: out0, out10, out11, out12, out13, out14, out15, out16, out17, out18, out19, out20, out21, out22, out23, out24, out25, out26, out27, out28, out29, out30, out31, en
  Register #(.width(32)) register_1 (.D(RW), .en(Write_Enable), .Q(at), .clk(Clock));  // open: clr
  Register #(.width(32)) register_2 (.D(RW), .Q(a1), .clk(Clock));  // open: en, clr
  Register #(.width(32)) register_3 (.D(RW), .Q(t1), .clk(Clock));  // open: en, clr
  Register #(.width(32)) register_4 (.D(RW), .Q(t5), .clk(Clock));  // open: en, clr
  Register #(.width(32)) register_5 (.D(RW), .Q(s1_Value), .clk(Clock));  // open: en, clr
  Register #(.width(32)) register_6 (.D(RW), .Q(t9), .clk(Clock));  // open: en, clr
  Register #(.width(32)) register_7 (.D(RW), .en(Write_Enable), .Q(v0), .clk(Clock));  // open: clr
  Register #(.width(32)) register_8 (.D(RW), .Q(a2), .clk(Clock));  // open: en, clr
  Register #(.width(32)) register_9 (.D(RW), .Q(t2), .clk(Clock));  // open: en, clr
  Register #(.width(32)) register_10 (.D(RW), .Q(t6), .clk(Clock));  // open: en, clr
  Register #(.width(32)) register_11 (.D(RW), .Q(s2_Value), .clk(Clock));  // open: en, clr
  Register #(.width(32)) register_12 (.D(RW), .Q(k0), .clk(Clock));  // open: en, clr
  Register #(.width(32)) register_13 (.D(RW), .en(Write_Enable), .Q(v1), .clk(Clock));  // open: clr
  Register #(.width(32)) register_14 (.D(RW), .Q(a3), .clk(Clock));  // open: en, clr
  Register #(.width(32)) register_15 (.D(RW), .Q(t3), .clk(Clock));  // open: en, clr
  Register #(.width(32)) register_16 (.D(RW), .Q(t7), .clk(Clock));  // open: en, clr
  Register #(.width(32)) register_17 (.D(RW), .Q(s3), .clk(Clock));  // open: en, clr
  Register #(.width(32)) register_18 (.D(RW), .Q(k1), .clk(Clock));  // open: en, clr
  Register #(.width(32)) register_19 (.D(RW), .en(Write_Enable), .Q(a0), .clk(Clock));  // open: clr
  Register #(.width(32)) register_20 (.D(RW), .Q(t0), .clk(Clock));  // open: en, clr
  Register #(.width(32)) register_21 (.D(RW), .Q(t4), .clk(Clock));  // open: en, clr
  Register #(.width(32)) register_22 (.D(RW), .Q(s0_Value), .clk(Clock));  // open: en, clr
  Register #(.width(32)) register_23 (.D(RW), .Q(s4), .clk(Clock));  // open: en, clr
  Register #(.width(32)) register_24 (.D(RW), .Q(gp), .clk(Clock));  // open: en, clr
  Register #(.width(32)) register_25 (.D(RW), .Q(s5), .clk(Clock));  // open: en, clr
  Register #(.width(32)) register_26 (.D(RW), .Q(sp_Value), .clk(Clock));  // open: en, clr
  Multiplexer #(.select(5), .width(32)) multiplexer_1 (
    .in1(at), .in2(v0), .in3(v1), .in4(a0), .in5(a1), .in6(a2), .out(Read_Data_1), .sel(Read_Register_1));  // open: in0, in7, in8, in9, in10, in11, in12, in13, in14, in15, in16, in17, in18, in19, in20, in21, in22, in23, in24, in25, in26, in27, in28, in29, in30, in31, en
  Register #(.width(32)) register_27 (.D(RW), .Q(s6), .clk(Clock));  // open: en, clr
  Register #(.width(32)) register_28 (.D(RW), .Q(fp), .clk(Clock));  // open: en, clr
  Register #(.width(32)) register_29 (.D(RW), .Q(s7), .clk(Clock));  // open: en, clr
  Register #(.width(32)) register_30 (.D(RW), .Q(ra_Value), .clk(Clock));  // open: en, clr
  Register #(.width(32)) register_31 (.D(RW), .Q(t8), .clk(Clock));  // open: en, clr

  // Other names for the same wires on the sheet: clk = Clock; ra[31:0] = ra_Value; read_data1[31:0] = Read_Data_1;
  //   read_data2[31:0] = Read_Data_2; read_reg1[4:0] = Read_Register_1; read_reg2[4:0] = Read_Register_2;
  //   s0[31:0] = s0_Value; s1[31:0] = s1_Value; s2[31:0] = s2_Value; sp[31:0] = sp_Value; write_en = Write_Enable;
  //   write_reg[4:0] = Write_Register

  // Notes on the sheet:
  //   INPUTS to your circuit
  //   DON'T CHANGE THE LOCATIONS OF THE INPUTS AND OUTPUTS!
  //   These are DEBUG/TEST outputs from your circuit.
  //   OUTPUTS from your circuit
endmodule
